# Fritzing sketch led_matrix_wiring (saved by Fritzing 0.9.4)
breadboards: 1

parts:
  8x8_LED_Modul_mit_MAX1 = 8x8 LED Modul mit MAX7219 [package=THT]
  Part1 = Arduino Uno (Rev3) - ICSP

nets:
  N1: 8x8_LED_Modul_mit_MAX1.VCC_Eingang, Part1.VIN
  N2: 8x8_LED_Modul_mit_MAX1.GND_Eingang, Part1.GND
  N3: 8x8_LED_Modul_mit_MAX1.DIN_Eingang, Part1.D12/MISO
  N4: 8x8_LED_Modul_mit_MAX1.CS_Eingang, Part1.D10_PWM/SS
  N5: 8x8_LED_Modul_mit_MAX1.CLK_Eingang, Part1.D11_PWM/MOSI
